# Fritzing sketch AA (saved by Fritzing 0.9.3b)

parts:
  Part1 = Adafruit I2C+SPI LCD Backpack [part_number="Adafruit #292"]
  U1 = LCD-16X2 [package=lcd-16x2_noholes]
  Part2 = Arduino Nano (Rev3.0)
  Part3 = MQ-3 breakout
  Part4 = MQ-9 breakout
  Part5 = MQ-7 breakout
  Part6 = MQ-4
  Part7 = MQ-9 breakout
  Part8 = MQ-9 breakout

nets:
  GND: Part1.GND, U1.VSS, U1.R_W
  VCC: Part1.VCC, U1.VDD, U1.A
  N1: Part1.CLOCK, Part2.A5
  N2: Part1.DATA, Part2.A4
  N3: Part1.CONTRAST, U1.VO
  N4: Part1.RS, U1.RS
  N5: Part1.E, U1.E
  N6: Part1.DB0, U1.DB0
  N7: Part1.DB1, U1.DB1
  N8: Part1.DB2, U1.DB2
  N9: Part1.DB3, U1.DB3
  N10: Part1.DB4, U1.DB4
  N11: Part1.DB5, U1.DB5
  N12: Part1.DB6, U1.DB6
  N13: Part1.DB7, U1.DB7
  N14: Part1.LEDK, U1.K
  GND_2: Part2.GND, Part8.GND
  5V: Part2.5V, Part8.VCC
  N15: Part2.A7, Part8.AO
  N16: Part2.A6, Part7.AO
  N17: Part2.A3, Part5.AO
  N18: Part2.A2, Part4.AO
  N19: Part2.A1, Part6.VCC
  N20: Part2.A0, Part3.AO

notes:
  MQ135
  MQ8

custom parts:
  Adafruit I2C+SPI LCD Backpack: LCD backpacks reduce the number of pins needed to connect to an LCD. LCDs are a fun and easy way to have your microcontroller project talk back to you. Character LCDs are common, and easy to get, available in tons of colors and sizes. We've written tutorials on using character LCDs with an Arduino (or similar microcontroller) but find that the number of pins necessary to control the LCD can be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
  MQ-3 breakout: Alcohol sensor is capable of detecting alcohol (ethanol) particles on itself and gives the information in digital form back to us to manipulate with it. SKU:101251 • Voltage: 5V DC • Power: max 750mW • Measurement range: 0.04-4mg/L
  MQ-9 breakout: SKU: 101284
  MQ-7 breakout: SKU: 101282
